# Fritzing sketch candyMagic_electricCircuit (saved by Fritzing 0.9.3b)
breadboards: 1

parts:
  Part1 = Arduino 101
  D1 = Diode [package=diode-1n4001]
  T1 = TMP36 Temperature Sensor [package="TO92 [THT]"]
  R1 = Resistor [tolerance=±5% resistance=270 package=THT]
  R2 = Rotary Potentiometer (Small) [maximum_resistance=100kΩ package=THT]
  M1 = DC Motor
  R3 = Resistor [tolerance=±5% resistance=1k package=THT]
  LED1 = LED - 5mm [color="Blue (430nm)" package="5 mm [THT]"]

nets:
  N1: Part1.A0, R2.wiper
  N2: Part1.D12/MISO, R1.Pin_0
  N3: Part1.D13/SCK, LED1.anode
  N4: Part1.GND, T1.+Vs, R3.Pin_1, LED1.cathode
  N5: Part1.5V, D1.C, R2.leg1, M1.pin_1
  N6: T1.Vout, R1.Pin_1
  N7: T1.GND, M1.pin_2
  N8: R2.leg2, R3.Pin_0

custom parts:
  Arduino 101: A learning and development board that delivers the performance and low-power consumption of the Intel® Curie™ Module with the simplicity of Arduino at an entry-level price. It keeps the same robust form factor and peripheral list of the UNO with the addition of onboard Bluetooth LE capabilities and a 6-axis accelerometer/gyro to help you easily expand your creativity into the connected world.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
